# Fritzing sketch lcdDisplay (saved by Fritzing 0.9.2b)
breadboards: 1

parts:
  元件1 = Arduino Uno (Rev3)
  LCD1 = LCD screen
  R1 = Resistor [tolerance=±5% resistance=1k package=THT]

nets:
  N1: 元件1.D11_PWM/MOSI, LCD1.E
  N2: 元件1.D12/MISO, LCD1.RS
  GND: 元件1.GND, LCD1.VSS, LCD1.LED-, R1.Pin_1
  N3: 元件1.D2, LCD1.DB7
  N4: 元件1.D3_PWM, LCD1.DB6
  N5: 元件1.D4, LCD1.DB5
  N6: 元件1.D5_PWM, LCD1.DB4
  5V: 元件1.5V, LCD1.VDD, LCD1.LED+
  N7: LCD1.V0, R1.Pin_0
