# Fritzing sketch lcdDisplay (saved by Fritzing 0.9.3b)
breadboards: 1

parts:
  元件1 = Arduino Uno (Rev3)
  LCD1 = LCD screen
  R1 = Resistor [tolerance=±5% resistance=1k package=THT]
  hc-sr1 = hc-sr04
  J1 = Basic Servo

nets:
  N1: 元件1.D9_PWM, J1.pulse
  N2: 元件1.D11_PWM/MOSI, LCD1.E
  N3: 元件1.D12/MISO, LCD1.RS
  N4: 元件1.D2, LCD1.DB7
  N5: 元件1.D3_PWM, LCD1.DB6
  N6: 元件1.D4, LCD1.DB5
  N7: 元件1.D5_PWM, LCD1.DB4
  N8: 元件1.D6_PWM, hc-sr1.Trig
  N9: 元件1.D7, hc-sr1.Echo
  VCC: 元件1.5V, LCD1.VDD, LCD1.LED+, hc-sr1.VCC, J1.vcc
  GND: 元件1.GND, LCD1.VSS, LCD1.LED-, R1.Pin_1, hc-sr1.GND, J1.gnd
  N10: LCD1.V0, R1.Pin_0
